# Fritzing sketch Fritzing Sketch (saved by Fritzing 1.0.2b)
breadboards: 1

parts:
  Raspberry_Pi_1 = Raspberry Pi 3 [part_number=RPI-3-V1.2]
  J1 = Piezo Speaker
  A1 = 2 channel relay module [package=THT]
  S1 = Pushbutton [package="[THT]"]
  R1 = Resistor [tolerance=±5% resistance=220 package="2010 [SMD]"]
  R2 = Resistor [tolerance=±5% resistance=220 package="2010 [SMD]"]
  LED1 = smd LED [color="Red (633nm)" package="0805 [SMD]"]
  LED2 = smd LED [color="Green (570nm)" package="1206 [SMD]"]

nets:
  3V3: Raspberry_Pi_1.3v3, Raspberry_Pi_1.5V, A1.pin_13
  N1: Raspberry_Pi_1.GPIO3, Raspberry_Pi_1.GND, Raspberry_Pi_1.GIPO21, J1.pin2, A1.pin_14, S1.Pin_3, S1.Pin_4, R1.Pin_1, R2.Pin_0, LED1.cathode, LED2.anode
  N2: Raspberry_Pi_1.GIPO17, S1.Pin_1, S1.Pin_2
  N3: Raspberry_Pi_1.GIPO22, Raspberry_Pi_1.GIPO23, R2.Pin_1, LED1.anode
  N4: Raspberry_Pi_1.GIPO26, A1.pin_15
  N5: Raspberry_Pi_1.GIPO18, R1.Pin_0, LED2.cathode

custom parts:
  2 channel relay module: 2 channel Relay Module 5V 12V 24V High and Low Level Trigger Relay Control With Optocoupler Two Way relays DC 5 V 12 V 24 V Volt.
